// Logisim project Projeto2.circ as structural Verilog: 2 circuits, main circuit main
module main (
  input  in_1,
  input  in_2,
  input  in_3,
  input  in_4,
  input  in_5,
  input  in_6
);

  wire _0b, _0c, _1f, _15, _16, _29, _33, _38, _46, clock_1_out;
  wire [7:0] PC_q;
  wire [15:0] IR_q, ram_1_data;

  Clock clock_1 (.out(clock_1_out));
  Counter PC (.load(in_1), .count(in_2), .Q(PC_q), .clk(clock_1_out), .clr(in_6));  // open: D, carry
  Register ACC ();  // open: D, en, Q, clk, clr
  RAM #(.dataWidth(16), .bus("separate")) ram_1 (
    .addr(PC_q), .data(ram_1_data), .str(in_3), .clk(clock_1_out), .ld(in_4), .clr(in_5));  // open: din, sel
  Register #(.width(16)) IR (.D(ram_1_data), .Q(IR_q), .clk(clock_1_out), .clr(in_6));  // open: en
  Seletor seletor_1 (
    .in_1(IR_q[0]), .in_2(IR_q[1]), .in_3(IR_q[2]), .in_4(IR_q[3]), .in_5(IR_q[4]), .in_6(IR_q[5]),
    .in_7(IR_q[6]), .in_8(IR_q[7]), ._0b(_0b), ._0c(_0c), ._33(_33), ._15(_15), ._38(_38), ._16(_16),
    ._46(_46), ._1f(_1f), ._29(_29));
endmodule

module Seletor (
  input  in_1,
  input  in_2,
  input  in_3,
  input  in_4,
  input  in_5,
  input  in_6,
  input  in_7,
  input  in_8,
  output _0b,
  output _0c,
  output _33,
  output _15,
  output _38,
  output _16,
  output _46,
  output _1f,
  output _29
);

  and u__0c (_0c, ~in_1, ~in_2, ~in_3, ~in_4, in_5, in_6, ~in_7, ~in_8);  // AND_Gate
  and u__15 (_15, ~in_1, ~in_2, ~in_3, in_4, ~in_5, in_6, ~in_7, in_8);  // AND_Gate
  and u__16 (_16, ~in_1, ~in_2, ~in_3, in_4, ~in_5, in_6, in_7, ~in_8);  // AND_Gate
  and u__1f (_1f, ~in_1, ~in_2, ~in_3, in_4, in_5, in_6, in_7, in_8);  // AND_Gate
  and u__29 (_29, ~in_1, ~in_2, in_3, ~in_4, ~in_5, in_6, in_7, ~in_8);  // AND_Gate
  and u__0b (_0b, ~in_1, ~in_2, ~in_3, ~in_4, in_5, ~in_6, in_7, in_8);  // AND_Gate
  and u__33 (_33, ~in_1, ~in_2, in_3, in_4, ~in_5, ~in_6, in_7, in_8);  // AND_Gate
  and u__38 (_38, ~in_1, ~in_2, in_3, in_4, in_5, ~in_6, ~in_7, ~in_8);  // AND_Gate
  and u__46 (_46, ~in_1, in_2, ~in_3, ~in_4, ~in_5, in_6, in_7, ~in_8);  // AND_Gate
endmodule
